// Logisim project NotGate.circ as structural Verilog: 1 circuit, main circuit main
module main (
  input  in_1,
  input  in_2,
  input  in_3,
  input  in_4
);

  wire NAND_2_out, NAND_out;

  LED led_1 (.in(NAND_out));
  nand NAND (NAND_out, in_1, in_2);
  LED led_2 (.in(NAND_2_out));
  nand NAND_2 (NAND_2_out, in_3, in_4);
endmodule
